# Fritzing sketch esquema_arduino (saved by Fritzing 0.9.2b)

parts:
  Parte1 = Arduino Uno (Rev3)
  LED1 = LED - 5mm [color="Red (633nm)" package="5 mm [THT]"]
  R1 = Resistor [tolerance=±5% resistance=220 package=THT]
  R2 = Photocell (LDR) [package=THT]

nets:
  N1: Parte1.A0, R2.pin_0
  N2: Parte1.D13/SCK, LED1.anode
  N3: Parte1.GND, LED1.cathode, R1.Pin_0
  N4: Parte1.5V, R2.pin_1

notes:
  Sensor analógico
  Actuador (LED)
  comunicación CDC
